// Digital circuit FSM.dig as structural Verilog
module FSM (
  input  [3:0] op,
  input  clk,
  output [3:0] out_3
);

  wire dipswitch_1_out;
  wire [7:0] U2_d, U3_d, U4_d;
  wire [11:8] interrupt_out;

  Counter #(.Bits(4)) counter_1 (.en(1'b1), .C(clk), .clr(dipswitch_1_out), .out(out_3));  // open: ovf
  DipSwitch dipswitch_1 (.out(dipswitch_1_out));
  DipSwitch interrupt (.out(interrupt_out[8]));
  DipSwitch op2 (.out(interrupt_out[9]));
  DipSwitch jcmp (.out(interrupt_out[10]));
  DipSwitch reset (.out(interrupt_out[11]));
  EEPROM #(.AddrBits(12), .Bits(8)) U2 (.A({interrupt_out, op, out_3}), .CS(1'b1), .WE(1'b0), .OE(1'b1), .D(U2_d));
  EEPROM #(.AddrBits(12), .Bits(8)) U3 (.A({interrupt_out, op, out_3}), .CS(1'b1), .WE(1'b0), .OE(1'b1), .D(U3_d));
  EEPROM #(.AddrBits(12), .Bits(8)) U4 (.A({interrupt_out, op, out_3}), .CS(1'b1), .WE(1'b0), .OE(1'b1), .D(U4_d));
  LED Crx (.in(U2_d[1]));
  LED Edip (.in(U2_d[3]));
  LED Erx (.in(U2_d[5]));
  LED Cmar (.in(U2_d[7]));
  LED Einstr (.in(U3_d[1]));
  LED nil (.in(U3_d[3]));
  LED pcdec (.in(U3_d[5]));
  LED csp_plus__plus (.in(U3_d[7]));
  LED sel1 (.in(U4_d[1]));
  LED nil_2 (.in(U4_d[3]));
  LED Ealu (.in(U4_d[5]));
  LED Cir (.in(U4_d[7]));
  LED Edata (.in(U2_d[0]));
  LED Cpc (.in(U2_d[2]));
  LED Epc (.in(U2_d[4]));
  LED Cdata (.in(U2_d[6]));
  LED pcinc (.in(U3_d[0]));
  LED Estack (.in(U3_d[2]));
  LED Cstack (.in(U3_d[4]));
  LED csp (.in(U3_d[6]));
  LED cp0 (.in(U4_d[0]));
  LED setsub (.in(U4_d[2]));
  LED sel0 (.in(U4_d[4]));
  LED cp1 (.in(U4_d[6]));

  // Notes on the sheet:
  //   contents of U2 (hex, n*v repeats v):
  //   ff,df,fd,6*ff,df,fd,7*ff,fd,7*ff,fd,6*ff,5f,9f,6*ff,5f,9f,6*ff
  //   ,5f,fc,6*ff,5f,fc,6*ff,df,df,fd,5*ff,df,df,fd,5*ff,df,fd,6*ff
  //   ,df,fd,6*ff,df,df,fd,5*ff,df,df,fd,5*ff,df,df,fd,5*ff,df,df,fd
  //   ,5*ff,df,df,fd,5*ff,df,df,fd,5*ff,df,df,fd,5*ff,df,df,fd,5*ff
  //   ,df,fd,6*ff,df,fd,6*ff,df,fd,6*ff,df,fd,6*ff,df,7*ff,df,8*ff,fd
  //   ,7*ff,fd,6*ff,db,7*ff,db,7*ff,df,7*ff,df,6*ff,ef,ff,f3,5*ff,ef
  //   ,ff,f3,5*ff,ef,ff,f3,5*ff,ef,ff,f3,5*ff,ef,ff,f3,5*ff,ef,ff,f3
  //   ,5*ff,ef,ff,f3,5*ff,ef,ff,f3,5*ff,ef,ff,f3,5*ff,ef,ff,f3,5*ff
  //   ,ef,ff,f3,5*ff,ef,ff,f3,5*ff,ef,ff,f3,5*ff,ef,ff,f3,5*ff,ef,ff
  //   ,f3,5*ff,ef,ff,f3,5*ff,ef,ff,f3,5*ff,ef,ff,f3,5*ff,ef,ff,f3,5*ff
  //   ,ef,ff,f3,5*ff,ef,ff,f3,5*ff,ef,ff,f3,5*ff,ef,ff,f3,5*ff,ef,ff
  //   ,f3,5*ff,ef,ff,f3,5*ff,ef,ff,f3,5*ff,ef,ff,f3,5*ff,ef,ff,f3,5*ff
  //   ,ef,ff,f3,5*ff,ef,ff,f3,5*ff,ef,ff,f3,5*ff,ef,ff,f3,6*ff,df,fd
  //   ,6*ff,df,fd,7*ff,fd,7*ff,fd,6*ff,5f,9f,6*ff,5f,9f,6*ff,5f,fc,6*ff
  //   ,5f,fc,6*ff,df,df,fd,5*ff,df,df,fd,5*ff,df,fd,6*ff,df,fd,6*ff
  //   ,df,df,fd,5*ff,df,df,fd,5*ff,df,df,fd,5*ff,df,df,fd,5*ff,df,df
  //   ,fd,5*ff,df,df,fd,5*ff,df,df,fd,5*ff,df,df,fd,5*ff,df,fd,6*ff
  //   ,df,fd,6*ff,df,fd,6*ff,df,fd,6*ff,ef,7*ff,ef,8*ff,fb,7*ff,fb,6*ff
  //   ,db,7*ff,db,7*ff,df,7*ff,df,6*ff,ef,ff,f3,5*ff,ef,ff,f3,5*ff,ef
  //   ,ff,f3,5*ff,ef,ff,f3,5*ff,ef,ff,f3,5*ff,ef,ff,f3,5*ff,ef,ff,f3
  //   ,5*ff,ef,ff,f3,5*ff,ef,ff,f3,5*ff,ef,ff,f3,5*ff,ef,ff,f3,5*ff
  //   ,ef,ff,f3,5*ff,ef,ff,f3,5*ff,ef,ff,f3,5*ff,ef,ff,f3,5*ff,ef,ff
  //   ,f3,5*ff,ef,ff,f3,5*ff,ef,ff,f3,5*ff,ef,ff,f3,5*ff,ef,ff,f3,5*ff
  //   ,ef,ff,f3,5*ff,ef,ff,f3,5*ff,ef,ff,f3,5*ff,ef,ff,f3,5*ff,ef,ff
  //   ,f3,5*ff,ef,ff,f3,5*ff,ef,ff,f3,5*ff,ef,ff,f3,5*ff,ef,ff,f3,5*ff
  //   ,ef,ff,f3,5*ff,ef,ff,f3,5*ff,ef,ff,f3,6*ff,df,fd,6*ff,df,fd,7*ff
  //   ,fd,7*ff,fd,6*ff,5f,9f,6*ff,5f,9f,6*ff,5f,fc,6*ff,5f,fc,6*ff,df,df
  //   ,fd,5*ff,df,df,fd,5*ff,df,fd,6*ff,df,fd,6*ff,df,df,fd,5*ff,df,df
  //   ,fd,5*ff,df,df,fd,5*ff,df,df,fd,5*ff,df,df,fd,5*ff,df,df,fd,5*ff
  //   ,df,df,fd,5*ff,df,df,fd,5*ff,df,fd,6*ff,df,fd,6*ff,df,fd,6*ff
  //   ,df,fd,6*ff,df,7*ff,df,8*ff,fd,7*ff,fd,6*ff,db,7*ff,db,7*ff,df
  //   ,db,6*ff,df,db,5*ff,ef,ff,f3,5*ff,ef,ff,f3,5*ff,ef,ff,f3,5*ff
  //   ,ef,ff,f3,5*ff,ef,ff,f3,5*ff,ef,ff,f3,5*ff,ef,ff,f3,5*ff,ef,ff
  //   ,f3,5*ff,ef,ff,f3,5*ff,ef,ff,f3,5*ff,ef,ff,f3,5*ff,ef,ff,f3,5*ff
  //   ,ef,ff,f3,5*ff,ef,ff,f3,5*ff,ef,ff,f3,5*ff,ef,ff,f3,5*ff,ef,ff
  //   ,f3,5*ff,ef,ff,f3,5*ff,ef,ff,f3,5*ff,ef,ff,f3,5*ff,ef,ff,f3,5*ff
  //   ,ef,ff,f3,5*ff,ef,ff,f3,5*ff,ef,ff,f3,5*ff,ef,ff,f3,5*ff,ef,ff
  //   ,f3,5*ff,ef,ff,f3,5*ff,ef,ff,f3,5*ff,ef,ff,f3,5*ff,ef,ff,f3,5*ff
  //   ,ef,ff,f3,5*ff,ef,ff,f3,6*ff,df,fd,6*ff,df,fd,7*ff,fd,7*ff,fd
  //   ,6*ff,5f,9f,6*ff,5f,9f,6*ff,5f,fc,6*ff,5f,fc,6*ff,df,df,fd,5*ff
  //   ,df,df,fd,5*ff,df,fd,6*ff,df,fd,6*ff,df,df,fd,5*ff,df,df,fd,5*ff
  //   ,df,df,fd,5*ff,df,df,fd,5*ff,df,df,fd,5*ff,df,df,fd,5*ff,df,df
  //   ,fd,5*ff,df,df,fd,5*ff,df,fd,6*ff,df,fd,6*ff,df,fd,6*ff,df,fd
  //   ,6*ff,ef,7*ff,ef,8*ff,fb,7*ff,fb,6*ff,db,7*ff,db,7*ff,df,db,6*ff
  //   ,df,db,5*ff,ef,ff,f3,5*ff,ef,ff,f3,5*ff,ef,ff,f3,5*ff,ef,ff,f3
  //   ,5*ff,ef,ff,f3,5*ff,ef,ff,f3,5*ff,ef,ff,f3,5*ff,ef,ff,f3,5*ff
  //   ,ef,ff,f3,5*ff,ef,ff,f3,5*ff,ef,ff,f3,5*ff,ef,ff,f3,5*ff,ef,ff
  //   ,f3,5*ff,ef,ff,f3,5*ff,ef,ff,f3,5*ff,ef,ff,f3,5*ff,ef,ff,f3,5*ff
  //   ,ef,ff,f3,5*ff,ef,ff,f3,5*ff,ef,ff,f3,5*ff,ef,ff,f3,5*ff,ef,ff
  //   ,f3,5*ff,ef,ff,f3,5*ff,ef,ff,f3,5*ff,ef,ff,f3,5*ff,ef,ff,f3,5*ff
  //   ,ef,ff,f3,5*ff,ef,ff,f3,5*ff,ef,ff,f3,5*ff,ef,ff,f3,5*ff,ef,ff
  //   ,f3,5*ff,ef,ff,f3,2053*ff
  //   contents of U3 (hex, n*v repeats v):
  //   f5,f7,f7,f6,4*f7,f5,f7,f7,f6,4*f7,f5,f6,f5,f6,4*f7,f5,f6,f5,f6
  //   ,4*f7,f5,f7,f7,f6,4*f7,f5,f7,f7,f6,4*f7,f5,f7,f7,f6,4*f7,f5,f7,f7
  //   ,f6,4*f7,f5,7*f7,f5,7*f7,f5,f7,f7,f6,4*f7,f5,f7,f7,f6,4*f7,f5
  //   ,7*f7,f5,7*f7,f5,7*f7,f5,7*f7,f5,7*f7,f5,7*f7,f5,7*f7,f5,7*f7
  //   ,f5,f7,f7,f6,4*f7,f5,f7,f7,f6,4*f7,f5,f7,f7,f6,4*f7,f5,f7,f7,f6
  //   ,4*f7,f5,e7,77,f6,4*f7,f5,e7,77,f6,4*f7,f5,b7,f3,f6,4*f7,f5,b7
  //   ,f3,f6,4*f7,f5,7*f7,f5,7*f7,f5,f7,f6,5*f7,f5,f7,f6,5*f7,e7,77
  //   ,6*f7,e7,77,6*f7,e7,77,6*f7,e7,77,6*f7,e7,77,6*f7,e7,77,6*f7,e7
  //   ,77,6*f7,e7,77,6*f7,e7,77,6*f7,e7,77,6*f7,e7,77,6*f7,e7,77,6*f7
  //   ,e7,77,6*f7,e7,77,6*f7,e7,77,6*f7,e7,77,6*f7,e7,77,6*f7,e7,77
  //   ,6*f7,e7,77,6*f7,e7,77,6*f7,e7,77,6*f7,e7,77,6*f7,e7,77,6*f7,e7
  //   ,77,6*f7,e7,77,6*f7,e7,77,6*f7,e7,77,6*f7,e7,77,6*f7,e7,77,6*f7
  //   ,e7,77,6*f7,e7,77,6*f7,e7,77,6*f7,f5,f7,f7,f6,4*f7,f5,f7,f7,f6
  //   ,4*f7,f5,f6,f5,f6,4*f7,f5,f6,f5,f6,4*f7,f5,f7,f7,f6,4*f7,f5,f7,f7
  //   ,f6,4*f7,f5,f7,f7,f6,4*f7,f5,f7,f7,f6,4*f7,f5,7*f7,f5,7*f7,f5
  //   ,f7,f7,f6,4*f7,f5,f7,f7,f6,4*f7,f5,7*f7,f5,7*f7,f5,7*f7,f5,7*f7
  //   ,f5,7*f7,f5,7*f7,f5,7*f7,f5,7*f7,f5,f7,f7,f6,4*f7,f5,f7,f7,f6
  //   ,4*f7,f5,f7,f7,f6,4*f7,f5,f7,f7,f6,4*f7,f5,e7,77,f6,4*f7,f5,e7
  //   ,77,f6,4*f7,f5,b7,f3,5*f7,f5,b7,f3,5*f7,f5,7*f7,f5,7*f7,f5,f7
  //   ,f6,5*f7,f5,f7,f6,5*f7,e7,77,6*f7,e7,77,6*f7,e7,77,6*f7,e7,77
  //   ,6*f7,e7,77,6*f7,e7,77,6*f7,e7,77,6*f7,e7,77,6*f7,e7,77,6*f7,e7
  //   ,77,6*f7,e7,77,6*f7,e7,77,6*f7,e7,77,6*f7,e7,77,6*f7,e7,77,6*f7
  //   ,e7,77,6*f7,e7,77,6*f7,e7,77,6*f7,e7,77,6*f7,e7,77,6*f7,e7,77
  //   ,6*f7,e7,77,6*f7,e7,77,6*f7,e7,77,6*f7,e7,77,6*f7,e7,77,6*f7,e7
  //   ,77,6*f7,e7,77,6*f7,e7,77,6*f7,e7,77,6*f7,e7,77,6*f7,e7,77,6*f7
  //   ,f5,f7,f7,f6,4*f7,f5,f7,f7,f6,4*f7,f5,f6,f5,f6,4*f7,f5,f6,f5,f6
  //   ,4*f7,f5,f7,f7,f6,4*f7,f5,f7,f7,f6,4*f7,f5,f7,f7,f6,4*f7,f5,f7,f7
  //   ,f6,4*f7,f5,7*f7,f5,7*f7,f5,f7,f7,f6,4*f7,f5,f7,f7,f6,4*f7,f5
  //   ,7*f7,f5,7*f7,f5,7*f7,f5,7*f7,f5,7*f7,f5,7*f7,f5,7*f7,f5,7*f7
  //   ,f5,f7,f7,f6,4*f7,f5,f7,f7,f6,4*f7,f5,f7,f7,f6,4*f7,f5,f7,f7,f6
  //   ,4*f7,f5,e7,77,f6,4*f7,f5,e7,77,f6,4*f7,f5,b7,f3,f6,4*f7,f5,b7
  //   ,f3,f6,4*f7,f5,7*f7,f5,7*f7,f5,7*f7,f5,7*f7,e7,77,6*f7,e7,77,6*f7
  //   ,e7,77,6*f7,e7,77,6*f7,e7,77,6*f7,e7,77,6*f7,e7,77,6*f7,e7,77
  //   ,6*f7,e7,77,6*f7,e7,77,6*f7,e7,77,6*f7,e7,77,6*f7,e7,77,6*f7,e7
  //   ,77,6*f7,e7,77,6*f7,e7,77,6*f7,e7,77,6*f7,e7,77,6*f7,e7,77,6*f7
  //   ,e7,77,6*f7,e7,77,6*f7,e7,77,6*f7,e7,77,6*f7,e7,77,6*f7,e7,77
  //   ,6*f7,e7,77,6*f7,e7,77,6*f7,e7,77,6*f7,e7,77,6*f7,e7,77,6*f7,e7
  //   ,77,6*f7,e7,77,6*f7,f5,f7,f7,f6,4*f7,f5,f7,f7,f6,4*f7,f5,f6,f5
  //   ,f6,4*f7,f5,f6,f5,f6,4*f7,f5,f7,f7,f6,4*f7,f5,f7,f7,f6,4*f7,f5
  //   ,f7,f7,f6,4*f7,f5,f7,f7,f6,4*f7,f5,7*f7,f5,7*f7,f5,f7,f7,f6,4*f7
  //   ,f5,f7,f7,f6,4*f7,f5,7*f7,f5,7*f7,f5,7*f7,f5,7*f7,f5,7*f7,f5,7*f7
  //   ,f5,7*f7,f5,7*f7,f5,f7,f7,f6,4*f7,f5,f7,f7,f6,4*f7,f5,f7,f7,f6
  //   ,4*f7,f5,f7,f7,f6,4*f7,f5,e7,77,f6,4*f7,f5,e7,77,f6,4*f7,f5,b7
  //   ,f3,5*f7,f5,b7,f3,5*f7,f5,7*f7,f5,7*f7,f5,7*f7,f5,7*f7,e7,77,6*f7
  //   ,e7,77,6*f7,e7,77,6*f7,e7,77,6*f7,e7,77,6*f7,e7,77,6*f7,e7,77
  //   ,6*f7,e7,77,6*f7,e7,77,6*f7,e7,77,6*f7,e7,77,6*f7,e7,77,6*f7,e7
  //   ,77,6*f7,e7,77,6*f7,e7,77,6*f7,e7,77,6*f7,e7,77,6*f7,e7,77,6*f7
  //   ,e7,77,6*f7,e7,77,6*f7,e7,77,6*f7,e7,77,6*f7,e7,77,6*f7,e7,77
  //   ,6*f7,e7,77,6*f7,e7,77,6*f7,e7,77,6*f7,e7,77,6*f7,e7,77,6*f7,e7
  //   ,77,6*f7,e7,77,6*f7,e7,77,2054*f7
  //   contents of U4 (hex, n*v repeats v):
  //   65,e4,c7,e1,4*e5,65,e4,c7,e1,4*e5,65,e5,e7,e1,4*e5,65,e5,e7,e1
  //   ,4*e5,65,f5,e5,e1,4*e5,65,f5,e5,e1,4*e5,65,e5,e7,e1,4*e5,65,e5
  //   ,e7,e1,4*e5,65,e4,b5,c7,4*e5,65,e4,b5,c7,4*e5,65,e4,c7,e1,4*e5
  //   ,65,e4,c7,e1,4*e5,65,e4,b5,c7,4*e5,65,e4,b5,c7,4*e5,65,e4,b5,c7
  //   ,4*e5,65,e4,b5,c7,4*e5,65,e4,b5,c7,4*e5,65,e4,b5,c7,4*e5,65,e4
  //   ,b5,c7,4*e5,65,e4,b5,c7,4*e5,65,e4,c7,e1,4*e5,65,e4,c7,e1,4*e5
  //   ,65,e4,c7,e1,4*e5,65,e4,c7,e1,4*e5,65,e5,e5,e1,4*e5,65,e5,e5,e1
  //   ,4*e5,65,e5,e7,e1,4*e5,65,e5,e7,e1,4*e5,65,e5,e1,5*e5,65,e5,e1
  //   ,5*e5,65,f5,e1,5*e5,65,f5,e1,8*e5,e1,7*e5,e1,7*e5,e1,7*e5,e1,7*e5
  //   ,e1,7*e5,e1,7*e5,e1,7*e5,e1,7*e5,e1,7*e5,e1,7*e5,e1,7*e5,e1,7*e5
  //   ,e1,7*e5,e1,7*e5,e1,7*e5,e1,7*e5,e1,7*e5,e1,7*e5,e1,7*e5,e1,7*e5
  //   ,e1,7*e5,e1,7*e5,e1,7*e5,e1,7*e5,e1,7*e5,e1,7*e5,e1,7*e5,e1,7*e5
  //   ,e1,7*e5,e1,7*e5,e1,7*e5,e1,4*e5,65,e4,c7,e1,4*e5,65,e4,c7,e1
  //   ,4*e5,65,e5,e7,e1,4*e5,65,e5,e7,e1,4*e5,65,f5,e5,e1,4*e5,65,f5
  //   ,e5,e1,4*e5,65,e5,e7,e1,4*e5,65,e5,e7,e1,4*e5,65,e4,b5,c7,4*e5
  //   ,65,e4,b5,c7,4*e5,65,e4,c7,e1,4*e5,65,e4,c7,e1,4*e5,65,e4,b5,c7
  //   ,4*e5,65,e4,b5,c7,4*e5,65,e4,b5,c7,4*e5,65,e4,b5,c7,4*e5,65,e4
  //   ,b5,c7,4*e5,65,e4,b5,c7,4*e5,65,e4,b5,c7,4*e5,65,e4,b5,c7,4*e5
  //   ,65,e4,c7,e1,4*e5,65,e4,c7,e1,4*e5,65,e4,c7,e1,4*e5,65,e4,c7,e1
  //   ,4*e5,65,e5,e5,e1,4*e5,65,e5,e5,e1,4*e5,65,e5,e5,e1,4*e5,65,e5,e5
  //   ,e1,4*e5,65,e5,e1,5*e5,65,e5,e1,5*e5,65,f5,e1,5*e5,65,f5,e1,8*e5
  //   ,e1,7*e5,e1,7*e5,e1,7*e5,e1,7*e5,e1,7*e5,e1,7*e5,e1,7*e5,e1,7*e5
  //   ,e1,7*e5,e1,7*e5,e1,7*e5,e1,7*e5,e1,7*e5,e1,7*e5,e1,7*e5,e1,7*e5
  //   ,e1,7*e5,e1,7*e5,e1,7*e5,e1,7*e5,e1,7*e5,e1,7*e5,e1,7*e5,e1,7*e5
  //   ,e1,7*e5,e1,7*e5,e1,7*e5,e1,7*e5,e1,7*e5,e1,7*e5,e1,7*e5,e1,4*e5
  //   ,65,e4,c7,e1,4*e5,65,e4,c7,e1,4*e5,65,e5,e7,e1,4*e5,65,e5,e7,e1
  //   ,4*e5,65,f5,e5,e1,4*e5,65,f5,e5,e1,4*e5,65,e5,e7,e1,4*e5,65,e5
  //   ,e7,e1,4*e5,65,e4,b5,c7,4*e5,65,e4,b5,c7,4*e5,65,e4,c7,e1,4*e5
  //   ,65,e4,c7,e1,4*e5,65,e4,b5,c7,4*e5,65,e4,b5,c7,4*e5,65,e4,b5,c7
  //   ,4*e5,65,e4,b5,c7,4*e5,65,e4,b5,c7,4*e5,65,e4,b5,c7,4*e5,65,e4
  //   ,b5,c7,4*e5,65,e4,b5,c7,4*e5,65,e4,c7,e1,4*e5,65,e4,c7,e1,4*e5
  //   ,65,e4,c7,e1,4*e5,65,e4,c7,e1,4*e5,65,e5,e5,e1,4*e5,65,e5,e5,e1
  //   ,4*e5,65,e5,e7,e1,4*e5,65,e5,e7,e1,4*e5,65,e5,e1,5*e5,65,e5,e1
  //   ,5*e5,65,f5,e5,e1,4*e5,65,f5,e5,e1,7*e5,e1,7*e5,e1,7*e5,e1,7*e5
  //   ,e1,7*e5,e1,7*e5,e1,7*e5,e1,7*e5,e1,7*e5,e1,7*e5,e1,7*e5,e1,7*e5
  //   ,e1,7*e5,e1,7*e5,e1,7*e5,e1,7*e5,e1,7*e5,e1,7*e5,e1,7*e5,e1,7*e5
  //   ,e1,7*e5,e1,7*e5,e1,7*e5,e1,7*e5,e1,7*e5,e1,7*e5,e1,7*e5,e1,7*e5
  //   ,e1,7*e5,e1,7*e5,e1,7*e5,e1,7*e5,e1,4*e5,65,e4,c7,e1,4*e5,65,e4
  //   ,c7,e1,4*e5,65,e5,e7,e1,4*e5,65,e5,e7,e1,4*e5,65,f5,e5,e1,4*e5
  //   ,65,f5,e5,e1,4*e5,65,e5,e7,e1,4*e5,65,e5,e7,e1,4*e5,65,e4,b5,c7
  //   ,4*e5,65,e4,b5,c7,4*e5,65,e4,c7,e1,4*e5,65,e4,c7,e1,4*e5,65,e4
  //   ,b5,c7,4*e5,65,e4,b5,c7,4*e5,65,e4,b5,c7,4*e5,65,e4,b5,c7,4*e5
  //   ,65,e4,b5,c7,4*e5,65,e4,b5,c7,4*e5,65,e4,b5,c7,4*e5,65,e4,b5,c7
  //   ,4*e5,65,e4,c7,e1,4*e5,65,e4,c7,e1,4*e5,65,e4,c7,e1,4*e5,65,e4
  //   ,c7,e1,4*e5,65,e5,e5,e1,4*e5,65,e5,e5,e1,4*e5,65,e5,e5,e1,4*e5
  //   ,65,e5,e5,e1,4*e5,65,e5,e1,5*e5,65,e5,e1,5*e5,65,f5,e5,e1,4*e5
  //   ,65,f5,e5,e1,7*e5,e1,7*e5,e1,7*e5,e1,7*e5,e1,7*e5,e1,7*e5,e1,7*e5
  //   ,e1,7*e5,e1,7*e5,e1,7*e5,e1,7*e5,e1,7*e5,e1,7*e5,e1,7*e5,e1,7*e5
  //   ,e1,7*e5,e1,7*e5,e1,7*e5,e1,7*e5,e1,7*e5,e1,7*e5,e1,7*e5,e1,7*e5
  //   ,e1,7*e5,e1,7*e5,e1,7*e5,e1,7*e5,e1,7*e5,e1,7*e5,e1,7*e5,e1,7*e5
  //   ,e1,7*e5,e1,2052*e5
endmodule
